// Logisim project a1_XOR.circ as structural Verilog: 1 circuit, main circuit main
module main (
  input  A,
  input  B,
  output A_XOR_B
);

  wire and_1_out, and_2_out, not_1_out, not_2_out;

  not not_1 (not_1_out, A);
  not not_2 (not_2_out, B);
  and and_1 (and_1_out, not_1_out, B);
  and and_2 (and_2_out, A, not_2_out);
  or or_1 (A_XOR_B, and_1_out, and_2_out);
endmodule
