// Logisim project a2_RSFlipflop.circ as structural Verilog: 1 circuit, main circuit main
module main (
  input  S,
  input  R,
  output Q,
  output not_Q
);

  wire nand_1_out, nand_2_out;

  not nand_1 (nand_1_out, S);  // NAND_Gate
  not nand_2 (nand_2_out, R);  // NAND_Gate
  nand nand_3 (Q, nand_1_out, not_Q);
  nand nand_4 (not_Q, Q, nand_2_out);

  // Notes on the sheet:
  //   RS-FlipFlop
endmodule
