// Logisim project a3_3bitvoll.circ as structural Verilog: 1 circuit, main circuit main
module main (
  input  a,
  input  in_2,
  input  in_3,
  input  b,
  output out_5,
  output out_6,
  output a___b
);

  wire and_1_out, and_2_out, and_3_out, xor_2_out;

  and and_1 (and_1_out, in_2, b);
  xor xor_1 (a___b, in_2, b);
  and and_2 (and_2_out, a, in_3);
  xor xor_2 (xor_2_out, a, in_3);
  and and_3 (and_3_out, and_1_out, xor_2_out);
  xor xor_3 (out_6, and_1_out, xor_2_out);
  or or_1 (out_5, and_2_out, and_3_out);

  // Notes on the sheet:
  //   2bit Volladdierer
endmodule
