// Logisim project RSBS - Arith.circ as structural Verilog: 4 circuits, main circuit main
module main (
  input  Auswahl_B,
  input  Auswahl_Komplement_B,
  input  A0,
  input  A1,
  input  A2,
  input  A3,
  input  B0,
  input  B1,
  input  B2,
  input  B3,
  output Q0,
  output Q1,
  output Q2,
  output Q3
);

  wire komplement_1_q0, komplement_1_q1, komplement_1_q2, komplement_1_q3, mux_1_q0, mux_1_q1, mux_1_q2,
       mux_1_q3;

  Komplement komplement_1 (
    .Plus1(Auswahl_Komplement_B), .D0(B0), .D1(B1), .D2(B2), .D3(B3), .Q0(komplement_1_q0),
    .Q1(komplement_1_q1), .Q2(komplement_1_q2), .Q3(komplement_1_q3));
  MUX mux_1 (
    .Select(Auswahl_B), .A0(B0), .B0(komplement_1_q0), .A1(B1), .B1(komplement_1_q1), .A2(B2),
    .B2(komplement_1_q2), .A3(B3), .B3(komplement_1_q3), .Q0(mux_1_q0), .Q1(mux_1_q1), .Q2(mux_1_q2),
    .Q3(mux_1_q3));
  Addierer addierer_1 (
    .A0(A0), .B0(mux_1_q0), .A1(A1), .B1(mux_1_q1), .A2(A2), .B2(mux_1_q2), .A3(A3), .B3(mux_1_q3), .Q0(Q0),
    .Q1(Q1), .Q2(Q2), .Q3(Q3));
endmodule

module Addierer (
  input  A0,
  input  B0,
  input  A1,
  input  B1,
  input  A2,
  input  B2,
  input  A3,
  input  B3,
  output Q0,
  output Q1,
  output Q2,
  output Q3
);

  wire and_1_out, and_2_out, and_3_out, and_4_out, and_5_out, and_6_out, and_7_out, or_1_out, or_2_out,
       or_3_out, xor_2_out, xor_3_out, xor_4_out;

  xor xor_1 (Q0, A0, B0);
  and and_1 (and_1_out, A0, B0);
  xor xor_2 (xor_2_out, A1, B1);
  and and_2 (and_2_out, A1, B1);
  xor xor_3 (xor_3_out, A2, B2);
  and and_3 (and_3_out, A2, B2);
  xor xor_4 (xor_4_out, A3, B3);
  and and_4 (and_4_out, A3, B3);
  xor xor_5 (Q1, and_1_out, xor_2_out);
  and and_5 (and_5_out, and_1_out, xor_2_out);
  or or_1 (or_1_out, and_5_out, and_2_out);
  xor xor_6 (Q2, or_1_out, xor_3_out);
  and and_6 (and_6_out, or_1_out, xor_3_out);
  or or_2 (or_2_out, and_6_out, and_3_out);
  xor xor_7 (Q3, or_2_out, xor_4_out);
  and and_7 (and_7_out, or_2_out, xor_4_out);
  or or_3 (or_3_out, and_7_out, and_4_out);

  // Notes on the sheet:
  //   Überlauf
endmodule

module MUX (
  input  Select,
  input  A0,
  input  B0,
  input  A1,
  input  B1,
  input  A2,
  input  B2,
  input  A3,
  input  B3,
  output Q0,
  output Q1,
  output Q2,
  output Q3
);

  wire and_1_out, and_2_out, and_3_out, and_4_out, and_5_out, and_6_out, and_7_out, and_8_out, not_1_out;

  not not_1 (not_1_out, Select);
  and and_1 (and_1_out, not_1_out, A0);
  and and_2 (and_2_out, B0, Select);
  and and_3 (and_3_out, not_1_out, A1);
  and and_4 (and_4_out, B1, Select);
  and and_5 (and_5_out, not_1_out, A2);
  and and_6 (and_6_out, B2, Select);
  and and_7 (and_7_out, not_1_out, A3);
  and and_8 (and_8_out, B3, Select);
  or or_1 (Q0, and_1_out, and_2_out);
  or or_2 (Q1, and_3_out, and_4_out);
  or or_3 (Q2, and_5_out, and_6_out);
  or or_4 (Q3, and_7_out, and_8_out);
endmodule

module Komplement (
  input  Plus1,
  input  D0,
  input  D1,
  input  D2,
  input  D3,
  output Q0,
  output Q1,
  output Q2,
  output Q3
);

  wire and_1_out, and_2_out, and_3_out, not_1_out, not_2_out, not_3_out, not_4_out;

  not not_1 (not_1_out, D0);
  not not_2 (not_2_out, D1);
  not not_3 (not_3_out, D2);
  not not_4 (not_4_out, D3);
  xor xor_1 (Q0, Plus1, not_1_out);
  and and_1 (and_1_out, Plus1, not_1_out);
  xor xor_2 (Q1, and_1_out, not_2_out);
  and and_2 (and_2_out, and_1_out, not_2_out);
  xor xor_3 (Q2, and_2_out, not_3_out);
  and and_3 (and_3_out, and_2_out, not_3_out);
  xor xor_4 (Q3, and_3_out, not_4_out);
endmodule
